# Fritzing sketch arduino-altimeter (saved by Fritzing 0.9.4)
circuit board: 4.6cm x 5.33cm
breadboards: 1

parts:
  J1 = Screw terminal - 2 pins [package=THT]
  R2 = Resistor [tolerance=±5% resistance=220 package=THT]
  D1 = Rectifier Diode [part_number=1N4001 package="300 mil [THT]"]
  Fuse1 = Fuse with Handler [part_number=Htc-15m]
  S1 = GY-BMEP280 Barometric Pressure Sensor - Breakout
  AUXD9 = mystery part, 2 pins [chip_label=D9]
  AUXD10 = mystery part, 2 pins [chip_label=D10]
  AUXD11 = mystery part, 2 pins [chip_label=D11]
  AUXA0 = mystery part, 2 pins [chip_label=A0]
  AUXRST = mystery part, 2 pins [chip_label=RST]
  UC1 = Arduino Nano 33 BLE Sense
  R1 = Resistor [tolerance=±5% resistance=220 package=THT]
  IC1 = 24LC01 [package=THT]
  D2 = Rectifier Diode [part_number=1N4001 package="300 mil [THT]"]
  AUXD12 = mystery part, 2 pins [chip_label=D12]

nets:
  GND: J1.pin1, R2.Pin_0, S1.GND, S1.SDO, AUXD9.pin1, AUXD10.pin1, AUXD11.pin1, AUXA0.pin1, AUXRST.pin1, UC1.GND, UC1.A7, IC1.0V, IC1.WP_-_Write_Protect, D2.anode, AUXD12.pin1
  N1: J1.pin2, Fuse1.Connector1
  BATTERY: R2.Pin_1, UC1.A6, R1.Pin_0
  VIN: D1.cathode, UC1.VIN, R1.Pin_1
  N2: D1.anode, Fuse1.Connector2, D2.cathode
  3.3V: S1.VCC, S1.CSB, UC1.3V3, IC1.+V
  SCL: S1.SCL, UC1.A5, IC1.SCL_-_I2C_Clock
  SDA: S1.SDA, UC1.A4, IC1.SDA_-_I2C_Data
  D9: AUXD9.pin2, UC1.D9~
  D10: AUXD10.pin2, UC1.D10~
  D11: AUXD11.pin2, UC1.D11/MOSI, UC1.+5V
  A0: AUXA0.pin2, UC1.A0
  RST: AUXRST.pin2, UC1.RESET
  D12: UC1.D12~/MISO, AUXD12.pin2

custom parts:
  GY-BMEP280 Barometric Pressure Sensor - Breakout: The BME280 is a chip which was originally designed for the next generation of smartphones. It is made up of a very accurate pressure sensor and an associated temperature sensor which helps calibrate the pressure readings. And just for fun they threw in a pretty solid humidity sensor in there as well! So with an I2C connection you have access to enough weather data to make some pretty good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
  Arduino Nano 33 BLE Sense: The Nano 33 BLE Sense (without headers) is Arduino’s 3.3V AI enabled board in the smallest available form factor: 45x18mm! The Arduino Nano 33 BLE Sense is a completely new board on a well-known form factor. It comes with a series of embedded sensors: 9 axis inertial sensor: what makes this board ideal for wearable devices humidity, and temperature sensor: to get highly accurate measurements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
